# Fritzing sketch TVBGone (saved by Fritzing 0.9.3b)
breadboards: 1

parts:
  Bauteil1 = Arduino Uno (Rev3)
  LED1 = smd LED [color="Infrared (940nm)" package="1206 [SMD]"]
  LED2 = smd LED [color="Infrared (940nm)" package="1206 [SMD]"]
  Q1 = NPN-Transistor [package="TO92 [THT]"]
  R1 = Resistor [tolerance=±5% resistance=10 package=THT]
  R2 = Resistor [tolerance=±5% resistance=47 package=THT]
  S1 = Pushbutton [package=THT]
  VCC1 = Battery block 9V  # not connected
  R3 = Resistor [tolerance=±5% resistance=1k package=THT]

nets:
  N1: Bauteil1.GND, Q1.C, S1.leg1, R3.Pin_1
  N2: Bauteil1.D2, S1.leg0
  N3: Bauteil1.D3_PWM, R2.Pin_1
  N4: Bauteil1.D5_PWM, R3.Pin_0
  N5: Bauteil1.VIN, LED1.anode, LED2.anode
  N6: LED1.cathode, LED2.cathode, R1.Pin_0
  N7: Q1.E, R1.Pin_1
  N8: Q1.B, R2.Pin_0

notes:
  Only when using EU-codes. Otherwise leave PIN 5 as it is
